# Fritzing sketch nano-schematic (saved by Fritzing 0.9.4)
breadboards: 1

parts:
  HARP_IN = DIN-5 jack (MIDI) [package=THT]
  MIDI_OUT = DIN-5 jack (MIDI) [package=THT]
  R1 = Resistor [tolerance=±5% resistance=220 package=THT]
  Part1 = Arduino Nano (Rev3.0)

nets:
  N1: HARP_IN.3, Part1.D2
  N2: HARP_IN.5, Part1.D3
  N3: HARP_IN.2, MIDI_OUT.2, Part1.GND
  N4: HARP_IN.4, R1.Pin_0, Part1.5V
  N5: HARP_IN.1, Part1.D6
  N6: MIDI_OUT.5, Part1.D11/MOSI
  N7: MIDI_OUT.4, R1.Pin_1
